# Fritzing sketch BikeTrainer (saved by Fritzing 0.9.3b)
circuit board: 8.46667cm x 5.64444cm
breadboards: 1

parts:
  R1 = Resistor [tolerance=±5% resistance=220 package=THT]
  R2 = Resistor [tolerance=±5% resistance=220 package=THT]
  Wheel = Reed switch [package=THT]
  Cadence = Reed switch [package=THT]
  aBikeTrainer = Arduino Uno (Rev3)
  LCD1 = LCD screen
  R3 = Rotary Potentiometer (Small) [maximum_resistance=100kΩ package=THT]
  S1 = Pushbutton [package="[THT]"]
  S2 = Pushbutton [package="[THT]"]
  S3 = Pushbutton [package="[THT]"]
  R4 = Resistor [tolerance=±5% resistance=220 package=THT]
  R5 = Resistor [tolerance=±5% resistance=220 package=THT]
  R6 = Resistor [tolerance=±5% resistance=220 package=THT]

nets:
  N1: R1.Pin_0, Cadence.pin_1, aBikeTrainer.A1
  GND: R1.Pin_1, R2.Pin_0, aBikeTrainer.GND, LCD1.VSS, LCD1.R/W, LCD1.LED-, R3.leg1, R4.Pin_1, R5.Pin_1, R6.Pin_1
  N2: R2.Pin_1, Wheel.pin_2, aBikeTrainer.A0
  5V: Wheel.pin_1, Cadence.pin_2, aBikeTrainer.5V, LCD1.VDD, LCD1.LED+, R3.leg2, S1.Pin_1, S1.Pin_2, S2.Pin_1, S2.Pin_2, S3.Pin_1, S3.Pin_2
  N3: aBikeTrainer.D8, S1.Pin_3, S1.Pin_4, R4.Pin_0
  N4: aBikeTrainer.D9_PWM, S3.Pin_3, S3.Pin_4, R5.Pin_0
  N5: aBikeTrainer.D10_PWM/SS, S2.Pin_3, S2.Pin_4, R6.Pin_0
  N6: aBikeTrainer.D11_PWM/MOSI, LCD1.E
  N7: aBikeTrainer.D12/MISO, LCD1.RS
  N8: aBikeTrainer.D2, LCD1.DB7
  N9: aBikeTrainer.D3_PWM, LCD1.DB6
  N10: aBikeTrainer.D4, LCD1.DB5
  N11: aBikeTrainer.D5_PWM, LCD1.DB4
  N12: LCD1.V0, R3.wiper

// code stored in the sketch: BikeTrainer.ino

